# Fritzing sketch prototype_1 (saved by Fritzing 0.9.4)
circuit board: 5.77178cm x 4.12133cm
breadboards: 1

parts:
  RGB = RGB LED (com. cathode, rgb) [package="5 mm [THT]"]
  BME280 = prefix0000
  PM2_5 = Sharp_GP2Y1010AU0F [part_number=GP2Y1010AU0F]
  R1 = Resistor [tolerance=±5% resistance=220 package="0603 [SMD]"]
  R2 = Resistor [tolerance=±5% resistance=220 package="0603 [SMD]"]
  R3 = Resistor [tolerance=±5% resistance=220 package="0603 [SMD]"]
  D1 = WeMos D1 Mini
  R4 = Resistor [tolerance=±5% resistance=220 package="0603 [SMD]"]
  C1 = Electrolytic Capacitor [capacitance=0.22mF voltage=16V package="0605 [SMD, electrolytic]"]

nets:
  N1: RGB.red_anode, R1.Pin_1
  N2: RGB.common_cathode, BME280.connector1, PM2_5.connector1, PM2_5.connector3, D1.G, C1.-
  N3: RGB.green_anode, R2.Pin_1
  N4: RGB.blue_anode, R3.Pin_0, R3.Pin_1, D1.D3
  N5: BME280.connector0, D1.5V
  N6: BME280.connector2, D1.D5
  N7: BME280.connector3, D1.D6
  N8: PM2_5.connector0, PM2_5.connector5, D1.3V3, R4.Pin_0, R4.Pin_1, C1.+
  N9: PM2_5.connector2, D1.D0
  N10: PM2_5.connector4, D1.A0
  N11: R1.Pin_0, D1.D2
  N12: R2.Pin_0, D1.D1

notes:
  skunk 0.1
