# Fritzing sketch prototype_BME280_DSM501 (saved by Fritzing 0.9.4)
circuit board: 4.19747cm x 3.49096cm
breadboards: 1

parts:
  Wemos_D1 = WeMos D1 Mini
  BME280 = BME280
  VCC1 = Battery
  DSM501A = male pin header, 5 pins [form="♂ (male)"]
  Step-Up = male pin header, 3 pins [form="♂ (male)"]

nets:
  3V3: Wemos_D1.3V3, BME280.VIN
  N1: Wemos_D1.5V, DSM501A.pin3, Step-Up.pin3
  N2: Wemos_D1.A0, VCC1.+, Step-Up.pin1
  N3: Wemos_D1.D1, BME280.SCL
  N4: Wemos_D1.D2, BME280.SDA
  N5: Wemos_D1.D5, DSM501A.pin4
  N6: Wemos_D1.D6, DSM501A.pin2
  N7: Wemos_D1.G, BME280.GND, VCC1.-, DSM501A.pin5, Step-Up.pin2

notes:
  +

custom parts:
  BME280: Temperature Humidity Barometric presure Sensor
