# Fritzing sketch prototype_BME280_GP2Y1010AU0F (saved by Fritzing 0.9.4)
circuit board: 4.19747cm x 3.49096cm
breadboards: 1

parts:
  Wemos_D1 = WeMos D1 Mini
  BME280 = BME280
  U1 = Sharp Dust Sensor [part_number=GP2Y1010AU0F]
  R1 = Resistor [tolerance=±2% resistance=150 package=THT]
  C1 = Electrolytic Capacitor [capacitance=0.22mF voltage=16V package="0605 [SMD, electrolytic]"]

nets:
  3V3: Wemos_D1.3V3, BME280.VIN, U1.VCC, R1.Pin_1
  N1: Wemos_D1.A0, U1.Vo
  N2: Wemos_D1.D1, BME280.SCL
  N3: Wemos_D1.D2, BME280.SDA
  N4: Wemos_D1.D5, U1.LED
  N5: Wemos_D1.G, BME280.GND, U1.LED-GND, U1.S-GND, C1.-
  N6: U1.V-LED, R1.Pin_0, C1.+

custom parts:
  BME280: Temperature Humidity Barometric presure Sensor
  Sharp Dust Sensor: Sharp GP2Y1010AU0F Dust Sensor
